// Logisim project Complete Circuit.circ as structural Verilog: 6 circuits, main circuit main
module main (
  output [3:0] RS,
  output [3:0] RT,
  output [15:0] out_3,
  output [15:0] out_4,
  output [15:0] out_5,
  output [3:0] RD
);

  wire alu_new_1_zero, and_1_out, Clock_out, control_unit_1_binv, control_unit_1_branch, control_unit_1_cin,
       control_unit_1_jump, control_unit_1_memread, control_unit_1_memtoreg, control_unit_1_memwrite,
       control_unit_1_ramen, control_unit_1_regdest, control_unit_1_rt_im, control_unit_1_writeen,
       RamClr_out, RegClr_out;
  wire [1:0] control_unit_1_aluop;
  wire [3:0] multiplexer_1_out;
  wire [15:0] adder_1_out, bit_extender_1_out, bit_extender_2_out, multiplexer_3_out, multiplexer_4_out,
       multiplexer_5_out, ram_1_data, register_1_q, register_file_1_read_data_2;
  wire [15:12] rom_1_data;

  Register #(.width(16)) register_1 (.D(multiplexer_4_out), .Q(register_1_q), .clk(Clock_out));  // open: en, clr
  Button Clock (.out(Clock_out));
  Button RegClr (.out(RegClr_out));
  Button RamClr (.out(RamClr_out));
  Adder #(.width(16)) adder_1 (.a(16'h1), .b(register_1_q), .out(adder_1_out));  // open: cin, cout
  ROM #(.addrWidth(16), .dataWidth(16)) rom_1 (.addr(register_1_q), .data({rom_1_data, RS, RT, RD}));  // open: sel
  assign bit_extender_1_out = {{4{1'b0}}, {RS, RT, RD}};  // Bit_Extender bit_extender_1
  Multiplexer #(.width(4), .enable("false")) multiplexer_1 (
    .in0(RD), .in1(RT), .out(multiplexer_1_out), .sel(control_unit_1_regdest));
  Control_Unit control_unit_1 (
    .in_1(rom_1_data), .AluOp(control_unit_1_aluop), .Cin(control_unit_1_cin), .Binv(control_unit_1_binv),
    .WriteEn(control_unit_1_writeen), .RamEn(control_unit_1_ramen), .MemWrite(control_unit_1_memwrite),
    .MemRead(control_unit_1_memread), .MemToReg(control_unit_1_memtoreg), .RegDest(control_unit_1_regdest),
    .RT_IM(control_unit_1_rt_im), .Branch(control_unit_1_branch), .Jump(control_unit_1_jump));
  Register_File register_file_1 (
    .Read_Register_1(RS), .Write_Register(multiplexer_1_out), .Read_Register_2(RT), .Read_Data_1(out_3),
    .Read_Data_2(register_file_1_read_data_2), .Write_Enable(control_unit_1_writeen),
    .Write_Data(multiplexer_5_out), .Clear(RegClr_out), .Clock(Clock_out));
  assign bit_extender_2_out = {{12{1'b0}}, RD};  // Bit_Extender bit_extender_2
  Multiplexer #(.width(16), .enable("false")) multiplexer_2 (
    .in0(register_file_1_read_data_2), .in1(bit_extender_2_out), .out(out_4), .sel(control_unit_1_rt_im));
  ALU_New alu_new_1 (
    .Cin(control_unit_1_cin), .ALUOP(control_unit_1_aluop), .Binv(control_unit_1_binv), .F(out_5), .A(out_3),
    .B(out_4), .Zero(alu_new_1_zero));  // open: Cout
  and and_1 (and_1_out, alu_new_1_zero, control_unit_1_branch);
  Multiplexer #(.width(16), .enable("false")) multiplexer_3 (
    .in0(adder_1_out), .in1(bit_extender_2_out), .out(multiplexer_3_out), .sel(and_1_out));
  Multiplexer #(.width(16), .enable("false")) multiplexer_4 (
    .in0(multiplexer_3_out), .in1(bit_extender_1_out), .out(multiplexer_4_out), .sel(control_unit_1_jump));
  RAM #(.addrWidth(16), .dataWidth(16), .bus("separate")) ram_1 (
    .addr(out_5), .din(register_file_1_read_data_2), .data(ram_1_data), .str(control_unit_1_memwrite),
    .sel(control_unit_1_ramen), .clk(Clock_out), .ld(control_unit_1_memread), .clr(RamClr_out));
  Multiplexer #(.width(16), .enable("false")) multiplexer_5 (
    .in0(out_5), .in1(ram_1_data), .out(multiplexer_5_out), .sel(control_unit_1_memtoreg));

  // Notes on the sheet:
  //   contents of rom_1 (hex, n*v repeats v):
  //   4123 6121
endmodule

module Register_File (
  input  Clear,
  input  [15:0] Write_Data,
  input  Clock,
  input  [3:0] Read_Register_1,
  input  [3:0] Write_Register,
  input  Write_Enable,
  input  [3:0] Read_Register_2,
  output [15:0] Read_Data_1,
  output [15:0] Read_Data_2
);

  wire and_1_out, and_2_out, and_3_out, and_4_out, and_5_out, and_6_out, and_7_out, and_8_out, and_9_out,
       and_10_out, and_11_out, and_12_out, and_13_out, and_14_out, and_15_out, and_16_out, decoder_1_out0,
       decoder_1_out1, decoder_1_out2, decoder_1_out3, decoder_1_out4, decoder_1_out5, decoder_1_out6,
       decoder_1_out7, decoder_1_out8, decoder_1_out9, decoder_1_out10, decoder_1_out11, decoder_1_out12,
       decoder_1_out13, decoder_1_out14, decoder_1_out15;
  wire [15:0] R0_q, R1_q, R2_q, R3_q, R4_q, R5_q, R6_q, R7_q, R8_q, R9_q, R10_q, R11_q, R12_q, R13_q, R14_q,
       R15_q;

  Decoder #(.select(4), .enable("false")) decoder_1 (
    .out0(decoder_1_out0), .out1(decoder_1_out1), .out2(decoder_1_out2), .out3(decoder_1_out3),
    .out4(decoder_1_out4), .out5(decoder_1_out5), .out6(decoder_1_out6), .out7(decoder_1_out7),
    .out8(decoder_1_out8), .out9(decoder_1_out9), .out10(decoder_1_out10), .out11(decoder_1_out11),
    .out12(decoder_1_out12), .out13(decoder_1_out13), .out14(decoder_1_out14), .out15(decoder_1_out15),
    .sel(Write_Register));
  and and_1 (and_1_out, decoder_1_out0, Write_Enable);
  buf and_2 (and_2_out, decoder_1_out1);  // AND_Gate
  and and_3 (and_3_out, decoder_1_out2, Write_Enable);
  and and_4 (and_4_out, decoder_1_out3, Write_Enable);
  and and_5 (and_5_out, decoder_1_out4, Write_Enable);
  and and_6 (and_6_out, decoder_1_out5, Write_Enable);
  and and_7 (and_7_out, decoder_1_out6, Write_Enable);
  and and_8 (and_8_out, decoder_1_out7, Write_Enable);
  and and_9 (and_9_out, decoder_1_out8, Write_Enable);
  and and_10 (and_10_out, decoder_1_out9, Write_Enable);
  and and_11 (and_11_out, decoder_1_out10, Write_Enable);
  and and_12 (and_12_out, decoder_1_out11, Write_Enable);
  and and_13 (and_13_out, decoder_1_out12, Write_Enable);
  and and_14 (and_14_out, decoder_1_out13, Write_Enable);
  and and_15 (and_15_out, decoder_1_out14, Write_Enable);
  and and_16 (and_16_out, decoder_1_out15, Write_Enable);
  Register #(.width(16)) R0 (.D(Write_Data), .en(and_1_out), .Q(R0_q), .clk(Clock), .clr(Clear));
  Register #(.width(16)) R1 (.D(Write_Data), .en(and_2_out), .Q(R1_q), .clk(Clock), .clr(Clear));
  Register #(.width(16)) R2 (.D(Write_Data), .en(and_3_out), .Q(R2_q), .clk(Clock), .clr(Clear));
  Register #(.width(16)) R3 (.D(Write_Data), .en(and_4_out), .Q(R3_q), .clk(Clock), .clr(Clear));
  Register #(.width(16)) R4 (.D(Write_Data), .en(and_5_out), .Q(R4_q), .clk(Clock), .clr(Clear));
  Register #(.width(16)) R5 (.D(Write_Data), .en(and_6_out), .Q(R5_q), .clk(Clock), .clr(Clear));
  Register #(.width(16)) R6 (.D(Write_Data), .en(and_7_out), .Q(R6_q), .clk(Clock), .clr(Clear));
  Register #(.width(16)) R7 (.D(Write_Data), .en(and_8_out), .Q(R7_q), .clk(Clock), .clr(Clear));
  Register #(.width(16)) R8 (.D(Write_Data), .en(and_9_out), .Q(R8_q), .clk(Clock), .clr(Clear));
  Register #(.width(16)) R9 (.D(Write_Data), .en(and_10_out), .Q(R9_q), .clk(Clock), .clr(Clear));
  Register #(.width(16)) R10 (.D(Write_Data), .en(and_11_out), .Q(R10_q), .clk(Clock), .clr(Clear));
  Register #(.width(16)) R11 (.D(Write_Data), .en(and_12_out), .Q(R11_q), .clk(Clock), .clr(Clear));
  Register #(.width(16)) R12 (.D(Write_Data), .en(and_13_out), .Q(R12_q), .clk(Clock), .clr(Clear));
  Register #(.width(16)) R13 (.D(Write_Data), .en(and_14_out), .Q(R13_q), .clk(Clock), .clr(Clear));
  Register #(.width(16)) R14 (.D(Write_Data), .en(and_15_out), .Q(R14_q), .clk(Clock), .clr(Clear));
  Register #(.width(16)) R15 (.D(Write_Data), .en(and_16_out), .Q(R15_q), .clk(Clock), .clr(Clear));
  Multiplexer #(.select(4), .width(16), .enable("false")) multiplexer_1 (
    .in0(R0_q), .in1(R1_q), .in2(R2_q), .in3(R3_q), .in4(R4_q), .in5(R5_q), .in6(R6_q), .in7(R7_q),
    .in8(R8_q), .in9(R9_q), .in10(R10_q), .in11(R11_q), .in12(R12_q), .in13(R13_q), .in14(R14_q),
    .in15(R15_q), .out(Read_Data_1), .sel(Read_Register_1));
  Multiplexer #(.select(4), .width(16), .enable("false")) multiplexer_2 (
    .in0(R0_q), .in1(R1_q), .in2(R2_q), .in3(R3_q), .in4(R4_q), .in5(R5_q), .in6(R6_q), .in7(R7_q),
    .in8(R8_q), .in9(R9_q), .in10(R10_q), .in11(R11_q), .in12(R12_q), .in13(R13_q), .in14(R14_q),
    .in15(R15_q), .out(Read_Data_2), .sel(Read_Register_2));
endmodule

module _1_bit_ALU (
  input  Cin,
  input  A,
  input  B,
  input  [1:0] ALUop,
  input  Binv,
  output S,
  output Cout
);

  wire adder_1_out, and_1_out, multiplexer_1_out, not_1_out, or_1_out;

  not not_1 (not_1_out, B);
  Multiplexer #(.enable("false")) multiplexer_1 (.in0(B), .in1(not_1_out), .out(multiplexer_1_out), .sel(Binv));
  and and_1 (and_1_out, A, B);
  or or_1 (or_1_out, A, B);
  Adder #(.width(1)) adder_1 (.a(A), .b(multiplexer_1_out), .out(adder_1_out), .cin(Cin), .cout(Cout));
  Multiplexer #(.select(2), .enable("false")) multiplexer_2 (
    .in0(and_1_out), .in1(or_1_out), .in2(adder_1_out), .out(S), .sel(ALUop));  // open: in3
endmodule

module _16_Bit_ALU (
  input  [15:0] B,
  input  Cin,
  input  [15:0] A,
  input  Binv,
  input  [1:0] in_5,
  output [15:0] S,
  output Zero,
  output Overflow,
  output Cout
);

  wire n1_bit_alu_1_cout, n1_bit_alu_2_cout, n1_bit_alu_3_cout, n1_bit_alu_4_cout, n1_bit_alu_5_cout,
       n1_bit_alu_6_cout, n1_bit_alu_7_cout, n1_bit_alu_8_cout, n1_bit_alu_9_cout, n1_bit_alu_10_cout,
       n1_bit_alu_11_cout, n1_bit_alu_12_cout, n1_bit_alu_13_cout, n1_bit_alu_14_cout, n1_bit_alu_15_cout;

  _1_bit_ALU u_1_bit_alu_1 (
    .Cin(Cin), .ALUop(in_5), .S(S[0]), .Cout(n1_bit_alu_1_cout), .A(A[0]), .B(B[0]), .Binv(Binv));
  _1_bit_ALU u_1_bit_alu_2 (
    .Cin(n1_bit_alu_1_cout), .ALUop(in_5), .S(S[1]), .Cout(n1_bit_alu_2_cout), .A(A[1]), .B(B[1]), .Binv(Binv));
  _1_bit_ALU u_1_bit_alu_3 (
    .Cin(n1_bit_alu_2_cout), .ALUop(in_5), .S(S[2]), .Cout(n1_bit_alu_3_cout), .A(A[2]), .B(B[2]), .Binv(Binv));
  _1_bit_ALU u_1_bit_alu_4 (
    .Cin(n1_bit_alu_3_cout), .ALUop(in_5), .S(S[3]), .Cout(n1_bit_alu_4_cout), .A(A[3]), .B(B[3]), .Binv(Binv));
  _1_bit_ALU u_1_bit_alu_5 (
    .Cin(n1_bit_alu_4_cout), .ALUop(in_5), .S(S[4]), .Cout(n1_bit_alu_5_cout), .A(A[4]), .B(B[4]), .Binv(Binv));
  _1_bit_ALU u_1_bit_alu_6 (
    .Cin(n1_bit_alu_5_cout), .ALUop(in_5), .S(S[5]), .Cout(n1_bit_alu_6_cout), .A(A[5]), .B(B[5]), .Binv(Binv));
  _1_bit_ALU u_1_bit_alu_7 (
    .Cin(n1_bit_alu_6_cout), .ALUop(in_5), .S(S[6]), .Cout(n1_bit_alu_7_cout), .A(A[6]), .B(B[6]), .Binv(Binv));
  _1_bit_ALU u_1_bit_alu_8 (
    .Cin(n1_bit_alu_7_cout), .ALUop(in_5), .S(S[7]), .Cout(n1_bit_alu_8_cout), .A(A[7]), .B(B[7]), .Binv(Binv));
  _1_bit_ALU u_1_bit_alu_9 (
    .Cin(n1_bit_alu_8_cout), .ALUop(in_5), .S(S[8]), .Cout(n1_bit_alu_9_cout), .A(A[8]), .B(B[8]), .Binv(Binv));
  _1_bit_ALU u_1_bit_alu_10 (
    .Cin(n1_bit_alu_9_cout), .ALUop(in_5), .S(S[9]), .Cout(n1_bit_alu_10_cout), .A(A[9]), .B(B[9]),
    .Binv(Binv));
  _1_bit_ALU u_1_bit_alu_11 (
    .Cin(n1_bit_alu_10_cout), .ALUop(in_5), .S(S[10]), .Cout(n1_bit_alu_11_cout), .A(A[10]), .B(B[10]),
    .Binv(Binv));
  _1_bit_ALU u_1_bit_alu_12 (
    .Cin(n1_bit_alu_11_cout), .ALUop(in_5), .S(S[11]), .Cout(n1_bit_alu_12_cout), .A(A[11]), .B(B[11]),
    .Binv(Binv));
  _1_bit_ALU u_1_bit_alu_13 (
    .Cin(n1_bit_alu_12_cout), .ALUop(in_5), .S(S[12]), .Cout(n1_bit_alu_13_cout), .A(A[12]), .B(B[12]),
    .Binv(Binv));
  _1_bit_ALU u_1_bit_alu_14 (
    .Cin(n1_bit_alu_13_cout), .ALUop(in_5), .S(S[13]), .Cout(n1_bit_alu_14_cout), .A(A[13]), .B(B[13]),
    .Binv(Binv));
  _1_bit_ALU u_1_bit_alu_15 (
    .Cin(n1_bit_alu_14_cout), .ALUop(in_5), .S(S[14]), .Cout(n1_bit_alu_15_cout), .A(A[14]), .B(B[14]),
    .Binv(Binv));
  _1_bit_ALU u_1_bit_alu_16 (
    .Cin(n1_bit_alu_15_cout), .ALUop(in_5), .S(S[15]), .Cout(Cout), .A(A[15]), .B(B[15]), .Binv(Binv));
  xor xor_1 (Overflow, n1_bit_alu_15_cout, Cout);
  nor nor_1 (Zero, S[0], S[1], S[2], S[3], S[4], S[5], S[6], S[7], S[8], S[9], S[10], S[11], S[12], S[13], S[14], S[15]);
endmodule

module ALU_New (
  input  [15:0] A,
  input  [15:0] B,
  input  [1:0] ALUOP,
  input  Cin,
  input  Binv,
  output [15:0] F,
  output Zero,
  output Cout
);

  wire comparator_1_lt;
  wire [3:0] bit_extender_1_out;
  wire [15:0] adder_1_out, and_1_out, bit_extender_2_out, multiplexer_1_out, not_1_out, shifter_1_out;

  Bit_Extender #(.in_width(16), .out_width(4)) bit_extender_1 (.in(B), .out(bit_extender_1_out));
  assign and_1_out = A & B;  // AND_Gate and_1, 16 bits wide
  Comparator #(.width(16)) comparator_1 (.a(A), .b(B), .eq(Zero), .lt(comparator_1_lt));  // open: gt
  Multiplexer #(.width(16), .enable("false")) multiplexer_1 (
    .in0(B), .in1(not_1_out), .out(multiplexer_1_out), .sel(Binv));
  assign not_1_out = ~B;  // NOT_Gate not_1, 16 bits wide
  Shifter #(.width(16)) shifter_1 (.in(A), .\dist (bit_extender_1_out), .out(shifter_1_out));
  assign bit_extender_2_out = {{15{1'b0}}, comparator_1_lt};  // Bit_Extender bit_extender_2
  Adder #(.width(16)) adder_1 (.a(A), .b(multiplexer_1_out), .out(adder_1_out), .cin(Cin), .cout(Cout));
  Multiplexer #(.select(2), .width(16), .enable("false")) multiplexer_2 (
    .in0(shifter_1_out), .in1(and_1_out), .in2(bit_extender_2_out), .in3(adder_1_out), .out(F), .sel(ALUOP));
endmodule

module Control_Unit (
  input  [3:0] in_1,
  output [1:0] AluOp,
  output Cin,
  output Binv,
  output WriteEn,
  output RamEn,
  output MemWrite,
  output MemRead,
  output MemToReg,
  output RegDest,
  output RT_IM,
  output Branch,
  output Jump
);

  wire decoder_1_out0, decoder_1_out1, decoder_1_out2, decoder_1_out4, decoder_1_out5, decoder_1_out6;

  Decoder #(.select(4), .enable("false")) decoder_1 (
    .out0(decoder_1_out0), .out1(decoder_1_out1), .out2(decoder_1_out2), .out3(MemRead),
    .out4(decoder_1_out4), .out5(decoder_1_out5), .out6(decoder_1_out6), .out7(Binv), .out8(MemWrite),
    .out9(Jump), .out10(Branch), .sel(in_1));  // open: out11, out12, out13, out14, out15
  or or_1 (AluOp[0], decoder_1_out2, MemRead, decoder_1_out5, decoder_1_out6, Binv, MemWrite);
  or or_2 (AluOp[1], MemRead, decoder_1_out4, decoder_1_out5, decoder_1_out6, Binv, MemWrite);
  or or_3 (WriteEn, decoder_1_out1, decoder_1_out2, MemRead, decoder_1_out4, decoder_1_out5, decoder_1_out6, Binv);
  or or_4 (RamEn, MemRead, MemWrite);
  or or_5 (RegDest, MemRead, decoder_1_out6);
  or or_6 (RT_IM, MemRead, decoder_1_out6, MemWrite);

  assign Cin = Binv;
  assign MemToReg = MemRead;
endmodule
